# Fritzing sketch fan_pwm (saved by Fritzing 0.9.4)
breadboards: 1

parts:
  Part1 = Arduino Uno (Rev3) - ICSP
  Q1 = NPN-Transistor [package="TO92 [THT]"]
  U1 = POT_SWITCH [package=pot_pth]
  Power_12V = Power plug
  R1 = Resistor [tolerance=±5% resistance=220 package=THT]
  M1 = DC Motor
  D1 = Rectifier Diode [part_number=1N4001 package="300 mil [THT]"]

nets:
  N1: Part1.A3, U1.G$2_1
  N2: Part1.5V, U1.G$1_A
  N3: Part1.D6_PWM, R1.Pin_1
  GND: Part1.GND, Q1.E, U1.G$1_E, Power_12V.GND
  N4: Q1.B, R1.Pin_0
  N5: Q1.C, M1.pin_2, D1.anode
  N6: Power_12V.VCC, M1.pin_1, D1.cathode
